// Logisim project project3.circ as structural Verilog: 3 circuits, main circuit main
// T0
module main (
  output [15:0] out_1
);

  wire and_1_out, and_2_out, and_3_out, and_4_out, and_5_out, and_6_out, and_7_out, and_8_out, and_9_out,
       and_10_out, and_11_out, and_12_out, and_13_out, and_14_out, and_15_out, and_16_out, and_17_out,
       and_18_out, and_19_out, and_20_out, and_21_out, and_22_out, and_23_out, and_24_out, and_25_out,
       and_26_out, and_27_out, and_28_out, and_29_out, and_30_out, and_31_out, and_32_out, and_33_out,
       and_34_out, and_35_out, and_36_out, and_37_out, and_38_out, and_39_out, and_40_out, and_41_out,
       and_42_out, and_43_out, and_44_out, and_45_out, and_46_out, and_47_out, and_48_out, and_49_out,
       and_50_out, and_51_out, and_52_out, and_53_out, and_54_out, and_55_out, and_56_out, and_57_out,
       and_58_out, and_59_out, and_60_out, clock_1_out, D0_LD, D1_ST, D2_MOV, D3_PSH, D4_PUL, D5_ADD, D6_SUB,
       D7_DEC, D8_INC, D9_AND, D10_OR, D11_NOT, D12_LSL, D13_LSR, D14_BRA, D15_BEQ, D16_BNE, D17_CALL,
       D18_RET, decoder_4_out0, decoder_4_out1, decoder_14_out0, decoder_14_out1, decoder_15_out0,
       decoder_15_out1, decoder_16_out0, decoder_16_out1, decoder_17_out0, decoder_17_out1, decoder_18_out0,
       decoder_18_out1, decoder_19_out0, decoder_19_out1, decoder_26_out0, decoder_26_out1, decoder_27_out0,
       decoder_27_out1, decoder_28_out0, decoder_28_out1, decoder_29_out0, decoder_29_out1, decoder_30_out0,
       decoder_30_out1, decoder_31_out0, decoder_31_out1, IR_EN, IR_LH, MEM_CLR, MEM_LD, MEM_SEL, MEM_STR,
       MuxCSel, not_1_out, not_2_out, not_3_out, not_4_out, not_5_out, not_6_out, not_7_out, not_8_out,
       not_9_out, not_10_out, not_11_out, not_12_out, not_13_out, not_14_out, not_15_out, not_16_out,
       not_17_out, not_18_out, not_19_out, not_20_out, not_21_out, not_22_out, not_23_out, not_24_out,
       not_25_out, not_26_out, not_27_out, not_28_out, not_29_out, not_30_out, not_31_out, not_32_out,
       not_33_out, not_34_out, not_35_out, not_36_out, not_37_out, or_2_out, or_3_out, or_4_out, or_5_out,
       or_12_out, or_17_out, SCR, T0, T1, T2, T3, T4, T5, T6, T7;
  wire [0:0] ALUFlags_t;
  wire [1:0] _3RB_FS, _4RB_FS, controlled_buffer_7_out, controlled_buffer_14_out, controlled_buffer_37_out,
       controlled_buffer_42_out, controlled_buffer_44_out, controlled_buffer_60_out,
       controlled_buffer_63_out, controlled_buffer_83_out, controlled_buffer_130_out,
       controlled_buffer_140_out, controlled_buffer_158_out, controlled_buffer_164_out,
       controlled_buffer_169_out, controlled_buffer_171_out, controlled_buffer_177_out,
       controlled_buffer_182_out, controlled_buffer_185_out, controlled_buffer_187_out,
       controlled_buffer_199_out, controlled_buffer_210_out, controlled_buffer_229_out,
       controlled_buffer_235_out, controlled_buffer_240_out, controlled_buffer_242_out,
       controlled_buffer_248_out, controlled_buffer_253_out, controlled_buffer_258_out,
       controlled_buffer_260_out, IR_FS, MuxASel, MuxBSel, OutASel, OutBSel, OutCSel, OutDSel;
  wire [2:0] controlled_buffer_128_out, controlled_buffer_134_out, controlled_buffer_149_out,
       controlled_buffer_152_out, controlled_buffer_154_out, controlled_buffer_156_out,
       controlled_buffer_208_out, controlled_buffer_214_out, controlled_buffer_220_out,
       controlled_buffer_223_out, controlled_buffer_226_out, controlled_buffer_228_out;
  wire [3:0] _3RB_RS, _4RB_RS, ALUFLags, ALUFS;

  counter counter_1 (
    .out_2(T0), .out_3(T1), .out_4(T2), .out_5(T3), .out_6(T4), .out_7(T5), .out_8(T6), .out_9(T7), .in_1(SCR));
  and and_1 (and_1_out, D14_BRA, T3);
  assign MuxBSel = and_1_out ? 2'b01 : 2'bz;  // Controlled_Buffer controlled_buffer_1
  assign _3RB_FS = and_1_out ? 2'b01 : 2'bz;  // Controlled_Buffer controlled_buffer_2
  assign _3RB_RS = and_1_out ? 4'b0001 : 4'bz;  // Controlled_Buffer controlled_buffer_3
  assign MEM_SEL = and_1_out ? 1'b0 : 1'bz;  // Controlled_Buffer controlled_buffer_4
  assign MEM_LD = and_1_out ? 1'b0 : 1'bz;  // Controlled_Buffer controlled_buffer_5
  assign MEM_STR = and_1_out ? 1'b0 : 1'bz;  // Controlled_Buffer controlled_buffer_6
  not not_1 (not_1_out, out_1[8]);
  and and_2 (and_2_out, D0_LD, not_1_out, T3);
  assign controlled_buffer_7_out = and_2_out ? out_1[10:9] : 2'bz;  // Controlled_Buffer controlled_buffer_7
  assign MuxASel = and_2_out ? 2'b00 : 2'bz;  // Controlled_Buffer controlled_buffer_8
  assign _4RB_FS = and_2_out ? 2'b01 : 2'bz;  // Controlled_Buffer controlled_buffer_9
  not not_2 (not_2_out, out_1[10]);
  and and_3 (and_3_out, D2_MOV, T3, not_2_out, not_3_out);
  assign OutASel = and_3_out ? out_1[6:5] : 2'bz;  // Controlled_Buffer controlled_buffer_10
  assign MuxCSel = and_3_out ? 1'b1 : 1'bz;  // Controlled_Buffer controlled_buffer_11
  assign ALUFS = and_3_out ? 4'b0000 : 4'bz;  // Controlled_Buffer controlled_buffer_12
  assign MuxASel = and_3_out ? 2'b11 : 2'bz;  // Controlled_Buffer controlled_buffer_13
  Decoder #(.select(2)) decoder_1 (
    .out0(_4RB_RS[0]), .out1(_4RB_RS[1]), .out2(_4RB_RS[2]), .out3(_4RB_RS[3]),
    .sel(controlled_buffer_14_out), .en(and_3_out));
  assign controlled_buffer_14_out = and_3_out ? out_1[9:8] : 2'bz;  // Controlled_Buffer controlled_buffer_14
  assign _4RB_FS = and_3_out ? 2'b01 : 2'bz;  // Controlled_Buffer controlled_buffer_15
  assign MEM_SEL = T0 ? 1'b1 : 1'bz;  // Controlled_Buffer controlled_buffer_16
  assign MEM_LD = T0 ? 1'b1 : 1'bz;  // Controlled_Buffer controlled_buffer_17
  assign _3RB_FS = T0 ? 2'b10 : 2'bz;  // Controlled_Buffer controlled_buffer_18
  assign _3RB_RS = T0 ? 4'b0001 : 4'bz;  // Controlled_Buffer controlled_buffer_19
  assign IR_EN = T0 ? 1'b1 : 1'bz;  // Controlled_Buffer controlled_buffer_20
  assign IR_FS = T0 ? 2'b11 : 2'bz;  // Controlled_Buffer controlled_buffer_21
  assign IR_LH = T0 ? 1'b0 : 1'bz;  // Controlled_Buffer controlled_buffer_22
  assign MEM_STR = T0 ? 1'b0 : 1'bz;  // Controlled_Buffer controlled_buffer_23
  assign OutDSel = T0 ? 2'b00 : 2'bz;  // Controlled_Buffer controlled_buffer_24
  assign MEM_CLR = T0 ? 1'b0 : 1'bz;  // Controlled_Buffer controlled_buffer_25
  Decoder #(.select(5), .enable("false")) decoder_2 (
    .out0(D0_LD), .out1(D1_ST), .out2(D2_MOV), .out3(D3_PSH), .out4(D4_PUL), .out5(D5_ADD), .out6(D6_SUB),
    .out7(D7_DEC), .out8(D8_INC), .out9(D9_AND), .out10(D10_OR), .out11(D11_NOT), .out12(D12_LSL),
    .out13(D13_LSR), .out14(D14_BRA), .out15(D15_BEQ), .out16(D16_BNE), .out17(D17_CALL), .out18(D18_RET),
    .sel(out_1[15:11]));  // open: out19, out20, out21, out22, out23, out24, out25, out26, out27, out28, out29, out30, out31
  Decoder #(.select(2)) decoder_3 (
    .out0(_4RB_RS[0]), .out1(_4RB_RS[1]), .out2(_4RB_RS[2]), .out3(_4RB_RS[3]),
    .sel(controlled_buffer_7_out), .en(and_2_out));
  not not_3 (not_3_out, out_1[7]);
  and and_4 (and_4_out, D14_BRA, T4);
  assign SCR = and_4_out ? 1'b1 : 1'bz;  // Controlled_Buffer controlled_buffer_26
  assign IR_LH = T1 ? 1'b1 : 1'bz;  // Controlled_Buffer controlled_buffer_27
  assign _3RB_RS = T1 ? 4'b0001 : 4'bz;  // Controlled_Buffer controlled_buffer_28
  assign OutDSel = T1 ? 2'b00 : 2'bz;  // Controlled_Buffer controlled_buffer_29
  assign MEM_SEL = T1 ? 1'b1 : 1'bz;  // Controlled_Buffer controlled_buffer_30
  assign MEM_LD = T1 ? 1'b1 : 1'bz;  // Controlled_Buffer controlled_buffer_31
  assign IR_EN = T1 ? 1'b1 : 1'bz;  // Controlled_Buffer controlled_buffer_32
  assign IR_FS = T1 ? 2'b11 : 2'bz;  // Controlled_Buffer controlled_buffer_33
  assign _3RB_FS = T1 ? 2'b10 : 2'bz;  // Controlled_Buffer controlled_buffer_34
  assign MEM_STR = T1 ? 1'b0 : 1'bz;  // Controlled_Buffer controlled_buffer_35
  assign MEM_CLR = T1 ? 1'b0 : 1'bz;  // Controlled_Buffer controlled_buffer_36
  and and_5 (and_5_out, D2_MOV, T3, out_1[10], out_1[7]);
  assign controlled_buffer_37_out = and_5_out ? out_1[6:5] : 2'bz;  // Controlled_Buffer controlled_buffer_37
  assign MuxASel = and_5_out ? 2'b10 : 2'bz;  // Controlled_Buffer controlled_buffer_38
  assign MuxCSel = and_5_out ? 1'b0 : 1'bz;  // Controlled_Buffer controlled_buffer_39
  assign ALUFS = and_5_out ? 4'b0000 : 4'bz;  // Controlled_Buffer controlled_buffer_40
  assign MuxBSel = and_5_out ? 2'b11 : 2'bz;  // Controlled_Buffer controlled_buffer_41
  assign controlled_buffer_42_out = and_5_out ? out_1[9:8] : 2'bz;  // Controlled_Buffer controlled_buffer_42
  assign _3RB_FS = and_5_out ? 2'b01 : 2'bz;  // Controlled_Buffer controlled_buffer_43
  and and_6 (and_6_out, D0_LD, out_1[8], T3);
  assign controlled_buffer_44_out = and_6_out ? out_1[10:9] : 2'bz;  // Controlled_Buffer controlled_buffer_44
  assign MuxASel = and_6_out ? 2'b01 : 2'bz;  // Controlled_Buffer controlled_buffer_45
  assign _4RB_FS = and_6_out ? 2'b01 : 2'bz;  // Controlled_Buffer controlled_buffer_46
  assign OutDSel = and_6_out ? 2'b01 : 2'bz;  // Controlled_Buffer controlled_buffer_47
  outcdecoder outcdecoder_1 (.in_1(controlled_buffer_37_out), .out_2(OutCSel));
  Decoder #(.select(2), .disabled(0)) decoder_4 (
    .out0(decoder_4_out0), .out1(decoder_4_out1), .out2(_3RB_RS[1]), .out3(_3RB_RS[2]),
    .sel(controlled_buffer_42_out), .en(and_5_out));
  or or_1 (_3RB_RS[0], decoder_4_out0, decoder_4_out1);
  and and_7 (and_7_out, D15_BEQ, ALUFlags_t[0]);
  assign IR_EN = T2 ? 1'b0 : 1'bz;  // Controlled_Buffer controlled_buffer_48
  Decoder #(.select(2)) decoder_5 (
    .out0(_4RB_RS[0]), .out1(_4RB_RS[1]), .out2(_4RB_RS[2]), .out3(_4RB_RS[3]),
    .sel(controlled_buffer_44_out), .en(and_6_out));
  not not_4 (not_4_out, ALUFlags_t[0]);
  and and_8 (and_8_out, not_4_out, D16_BNE);
  or or_2 (or_2_out, and_7_out, and_8_out);
  and and_9 (and_9_out, or_2_out, T3);
  assign MuxBSel = and_9_out ? 2'b01 : 2'bz;  // Controlled_Buffer controlled_buffer_49
  assign _3RB_FS = and_9_out ? 2'b01 : 2'bz;  // Controlled_Buffer controlled_buffer_50
  assign _4RB_RS = and_9_out ? 4'b0001 : 4'bz;  // Controlled_Buffer controlled_buffer_51
  assign MEM_SEL = and_9_out ? 1'b0 : 1'bz;  // Controlled_Buffer controlled_buffer_52
  assign MEM_LD = and_9_out ? 1'b0 : 1'bz;  // Controlled_Buffer controlled_buffer_53
  assign MEM_STR = and_9_out ? 1'b0 : 1'bz;  // Controlled_Buffer controlled_buffer_54
  or or_3 (or_3_out, D15_BEQ, D16_BNE);
  assign MEM_SEL = D0_LD ? 1'b1 : 1'bz;  // Controlled_Buffer controlled_buffer_55
  assign MEM_LD = D0_LD ? 1'b1 : 1'bz;  // Controlled_Buffer controlled_buffer_56
  assign MEM_STR = D0_LD ? 1'b0 : 1'bz;  // Controlled_Buffer controlled_buffer_57
  and and_10 (and_10_out, or_3_out, T4);
  assign SCR = and_10_out ? 1'b1 : 1'bz;  // Controlled_Buffer controlled_buffer_58
  Clock clock_1 (.out(clock_1_out));
  and and_11 (and_11_out, D0_LD, T4);
  assign SCR = and_11_out ? 1'b1 : 1'bz;  // Controlled_Buffer controlled_buffer_59
  not not_5 (not_5_out, out_1[10]);
  and and_12 (and_12_out, D2_MOV, T3, not_5_out, out_1[7]);
  assign controlled_buffer_60_out = and_12_out ? out_1[6:5] : 2'bz;  // Controlled_Buffer controlled_buffer_60
  assign MuxASel = and_12_out ? 2'b10 : 2'bz;  // Controlled_Buffer controlled_buffer_61
  assign _4RB_FS = and_12_out ? 2'b01 : 2'bz;  // Controlled_Buffer controlled_buffer_62
  Decoder #(.select(2)) decoder_6 (
    .out0(_4RB_RS[0]), .out1(_4RB_RS[1]), .out2(_4RB_RS[2]), .out3(_4RB_RS[3]),
    .sel(controlled_buffer_63_out), .en(and_12_out));
  assign controlled_buffer_63_out = and_12_out ? out_1[9:8] : 2'bz;  // Controlled_Buffer controlled_buffer_63
  outcdecoder outcdecoder_2 (.in_1(controlled_buffer_60_out), .out_2(OutCSel));
  and and_13 (and_13_out, D17_CALL, T3);
  assign MuxCSel = and_13_out ? 1'b0 : 1'bz;  // Controlled_Buffer controlled_buffer_64
  assign MuxASel = and_13_out ? 2'b10 : 2'bz;  // Controlled_Buffer controlled_buffer_65
  assign _3RB_FS = and_13_out ? 2'b01 : 2'bz;  // Controlled_Buffer controlled_buffer_66
  assign _3RB_RS = and_13_out ? 4'b0001 : 4'bz;  // Controlled_Buffer controlled_buffer_67
  assign MEM_SEL = and_13_out ? 1'b1 : 1'bz;  // Controlled_Buffer controlled_buffer_68
  assign MEM_LD = and_13_out ? 1'b1 : 1'bz;  // Controlled_Buffer controlled_buffer_69
  assign MEM_STR = and_13_out ? 1'b1 : 1'bz;  // Controlled_Buffer controlled_buffer_70
  assign OutDSel = and_13_out ? 2'b10 : 2'bz;  // Controlled_Buffer controlled_buffer_71
  assign OutCSel = and_13_out ? 2'b00 : 2'bz;  // Controlled_Buffer controlled_buffer_72
  assign MuxBSel = and_13_out ? 2'b01 : 2'bz;  // Controlled_Buffer controlled_buffer_73
  assign ALUFS = and_13_out ? 4'b0000 : 4'bz;  // Controlled_Buffer controlled_buffer_74
  part2_main main_1 (
    .OutASel(OutASel), .OutBSel(OutBSel), .FunSel_2(_4RB_FS), .RegSel(_4RB_RS), .MuxASel(MuxASel),
    .OutCSel(OutCSel), .OutDSel(OutDSel), .FunSel_3(_3RB_FS), .RegSel_2(_3RB_RS), .L_H(IR_LH),
    .Enable(IR_EN), .FunSel_4(IR_FS), .MuxCSel(MuxCSel), .MuxBSel(MuxBSel), .FunSel(ALUFS), .in_10(MEM_STR),
    .in_11(MEM_SEL), .in_12(MEM_LD), .in_13(MEM_CLR), .out_22(ALUFLags), .out_23(out_1), .in_2(clock_1_out));  // open: out_21
  and and_14 (and_14_out, D17_CALL, T4);
  assign _3RB_FS = and_14_out ? 2'b11 : 2'bz;  // Controlled_Buffer controlled_buffer_75
  assign _3RB_RS = and_14_out ? 4'b0100 : 4'bz;  // Controlled_Buffer controlled_buffer_76
  assign MEM_STR = and_14_out ? 1'b0 : 1'bz;  // Controlled_Buffer controlled_buffer_77
  assign MuxBSel = and_14_out ? 2'b01 : 2'bz;  // Controlled_Buffer controlled_buffer_78
  Hex_Digit_Display hex_digit_display_1 (.value(out_1[15:12]));  // open: dp
  assign MEM_SEL = D2_MOV ? 1'b0 : 1'bz;  // Controlled_Buffer controlled_buffer_79
  assign MEM_LD = D2_MOV ? 1'b0 : 1'bz;  // Controlled_Buffer controlled_buffer_80
  assign MEM_STR = D2_MOV ? 1'b0 : 1'bz;  // Controlled_Buffer controlled_buffer_81
  and and_15 (and_15_out, D17_CALL, T5);
  assign SCR = and_15_out ? 1'b1 : 1'bz;  // Controlled_Buffer controlled_buffer_82
  Hex_Digit_Display hex_digit_display_2 (.value(out_1[11:8]));  // open: dp
  Hex_Digit_Display hex_digit_display_3 (.value(out_1[7:4]));  // open: dp
  Hex_Digit_Display hex_digit_display_4 (.value(out_1[3:0]));  // open: dp
  and and_16 (and_16_out, D1_ST, out_1[8], T3);
  assign controlled_buffer_83_out = and_16_out ? out_1[10:9] : 2'bz;  // Controlled_Buffer controlled_buffer_83
  Decoder #(.select(2)) decoder_7 (
    .out0(_4RB_RS[0]), .out1(_4RB_RS[1]), .out2(_4RB_RS[2]), .out3(_4RB_RS[3]),
    .sel(controlled_buffer_83_out), .en(and_16_out));
  assign OutBSel = and_16_out ? out_1[10:9] : 2'bz;  // Controlled_Buffer controlled_buffer_84
  assign ALUFS = and_16_out ? 4'b0000 : 4'bz;  // Controlled_Buffer controlled_buffer_85
  assign OutDSel = and_16_out ? 2'b01 : 2'bz;  // Controlled_Buffer controlled_buffer_86
  and and_17 (and_17_out, D18_RET, T3);
  assign _3RB_FS = and_17_out ? 2'b10 : 2'bz;  // Controlled_Buffer controlled_buffer_87
  assign _3RB_RS = and_17_out ? 4'b0100 : 4'bz;  // Controlled_Buffer controlled_buffer_88
  assign MEM_SEL = D1_ST ? 1'b1 : 1'bz;  // Controlled_Buffer controlled_buffer_89
  assign MEM_LD = D1_ST ? 1'b1 : 1'bz;  // Controlled_Buffer controlled_buffer_90
  assign MEM_STR = D1_ST ? 1'b1 : 1'bz;  // Controlled_Buffer controlled_buffer_91
  and and_18 (and_18_out, D18_RET, T4);
  assign OutDSel = and_18_out ? 2'b10 : 2'bz;  // Controlled_Buffer controlled_buffer_92
  assign MuxBSel = and_18_out ? 2'b10 : 2'bz;  // Controlled_Buffer controlled_buffer_93
  assign _3RB_FS = and_18_out ? 2'b01 : 2'bz;  // Controlled_Buffer controlled_buffer_94
  assign _3RB_RS = and_18_out ? 4'b0001 : 4'bz;  // Controlled_Buffer controlled_buffer_95
  assign MEM_SEL = and_18_out ? 1'b1 : 1'bz;  // Controlled_Buffer controlled_buffer_96
  assign MEM_LD = and_18_out ? 1'b1 : 1'bz;  // Controlled_Buffer controlled_buffer_97
  and and_19 (and_19_out, D18_RET, T5);
  assign SCR = and_19_out ? 1'b1 : 1'bz;  // Controlled_Buffer controlled_buffer_98
  and and_20 (and_20_out, D1_ST, T4);
  assign SCR = and_20_out ? 1'b1 : 1'bz;  // Controlled_Buffer controlled_buffer_99
  or or_4 (or_4_out, out_1[2], out_1[3], out_1[4]);
  and and_21 (and_21_out, D5_ADD, T2, out_1[7]);
  not not_6 (not_6_out, or_4_out);
  and and_22 (and_22_out, and_21_out, or_4_out);
  and and_23 (and_23_out, and_21_out, not_6_out);
  assign MuxASel = and_23_out ? 2'b10 : 2'bz;  // Controlled_Buffer controlled_buffer_100
  assign _4RB_FS = and_23_out ? 2'b01 : 2'bz;  // Controlled_Buffer controlled_buffer_101
  assign _4RB_RS = and_23_out ? 4'b0010 : 4'bz;  // Controlled_Buffer controlled_buffer_102
  assign OutCSel = and_23_out ? out_1[6:5] : 2'bz;  // Controlled_Buffer controlled_buffer_103
  assign OutASel = and_23_out ? 2'b10 : 2'bz;  // Controlled_Buffer controlled_buffer_104
  assign MuxASel = and_22_out ? 2'b10 : 2'bz;  // Controlled_Buffer controlled_buffer_105
  assign _4RB_FS = and_22_out ? 2'b01 : 2'bz;  // Controlled_Buffer controlled_buffer_106
  assign OutCSel = and_22_out ? out_1[6:5] : 2'bz;  // Controlled_Buffer controlled_buffer_107
  assign _4RB_RS = and_22_out ? 4'b0001 : 4'bz;  // Controlled_Buffer controlled_buffer_108
  assign OutASel = and_22_out ? 2'b01 : 2'bz;  // Controlled_Buffer controlled_buffer_109
  and and_24 (and_24_out, D5_ADD, T3, out_1[4]);
  or or_5 (or_5_out, out_1[2], out_1[3], out_1[4]);
  not not_7 (not_7_out, or_5_out);
  and and_25 (and_25_out, and_24_out, or_5_out);
  and and_26 (and_26_out, and_24_out, not_7_out);
  assign MuxASel = and_26_out ? 2'b10 : 2'bz;  // Controlled_Buffer controlled_buffer_110
  assign _4RB_FS = and_26_out ? 2'b01 : 2'bz;  // Controlled_Buffer controlled_buffer_111
  assign _4RB_RS = and_26_out ? 4'b0010 : 4'bz;  // Controlled_Buffer controlled_buffer_112
  assign OutCSel = and_26_out ? out_1[6:5] : 2'bz;  // Controlled_Buffer controlled_buffer_113
  assign OutASel = and_26_out ? 2'b10 : 2'bz;  // Controlled_Buffer controlled_buffer_114
  assign MuxASel = and_25_out ? 2'b10 : 2'bz;  // Controlled_Buffer controlled_buffer_115
  assign _4RB_FS = and_25_out ? 2'b01 : 2'bz;  // Controlled_Buffer controlled_buffer_116
  assign OutCSel = and_25_out ? out_1[6:5] : 2'bz;  // Controlled_Buffer controlled_buffer_117
  assign _4RB_RS = and_25_out ? 4'b0001 : 4'bz;  // Controlled_Buffer controlled_buffer_118
  assign OutASel = and_25_out ? 2'b01 : 2'bz;  // Controlled_Buffer controlled_buffer_119
  assign MEM_SEL = D8_INC ? 1'b0 : 1'bz;  // Controlled_Buffer controlled_buffer_120
  assign MEM_LD = D8_INC ? 1'b0 : 1'bz;  // Controlled_Buffer controlled_buffer_121
  assign MEM_STR = D8_INC ? 1'b0 : 1'bz;  // Controlled_Buffer controlled_buffer_122
  assign MEM_CLR = D8_INC ? 1'b0 : 1'bz;  // Controlled_Buffer controlled_buffer_123
  not not_8 (not_8_out, out_1[7]);
  and and_27 (and_27_out, not_8_out, D8_INC, T3, not_9_out);
  assign OutASel = and_27_out ? out_1[6:5] : 2'bz;  // Controlled_Buffer controlled_buffer_124
  assign MuxCSel = and_27_out ? 1'b1 : 1'bz;  // Controlled_Buffer controlled_buffer_125
  assign ALUFS = and_27_out ? 4'b0000 : 4'bz;  // Controlled_Buffer controlled_buffer_126
  assign MuxASel = and_27_out ? 2'b11 : 2'bz;  // Controlled_Buffer controlled_buffer_127
  Decoder #(.select(3)) decoder_8 (
    .out0(_4RB_RS[0]), .out1(_4RB_RS[1]), .out2(_4RB_RS[2]), .out3(_4RB_RS[3]),
    .sel(controlled_buffer_128_out), .en(and_27_out));  // open: out4, out5, out6, out7
  assign controlled_buffer_128_out = and_27_out ? out_1[10:8] : 3'bz;  // Controlled_Buffer controlled_buffer_128
  assign _4RB_FS = and_27_out ? 2'b01 : 2'bz;  // Controlled_Buffer controlled_buffer_129
  and and_28 (and_28_out, out_1[7], D8_INC, T3, not_10_out);
  assign controlled_buffer_130_out = and_28_out ? out_1[6:5] : 2'bz;  // Controlled_Buffer controlled_buffer_130
  assign MuxASel = and_28_out ? 2'b10 : 2'bz;  // Controlled_Buffer controlled_buffer_131
  assign MuxCSel = and_28_out ? 1'b0 : 1'bz;  // Controlled_Buffer controlled_buffer_132
  assign _4RB_FS = and_28_out ? 2'b01 : 2'bz;  // Controlled_Buffer controlled_buffer_133
  assign controlled_buffer_134_out = and_28_out ? out_1[10:8] : 3'bz;  // Controlled_Buffer controlled_buffer_134
  assign _4RB_FS = and_28_out ? 2'b01 : 2'bz;  // Controlled_Buffer controlled_buffer_135
  assign MEM_SEL = D12_LSL ? 1'b0 : 1'bz;  // Controlled_Buffer controlled_buffer_136
  assign MEM_LD = D12_LSL ? 1'b0 : 1'bz;  // Controlled_Buffer controlled_buffer_137
  assign MEM_STR = D12_LSL ? 1'b0 : 1'bz;  // Controlled_Buffer controlled_buffer_138
  assign MEM_CLR = D12_LSL ? 1'b0 : 1'bz;  // Controlled_Buffer controlled_buffer_139
  not not_9 (not_9_out, out_1[10]);
  not not_10 (not_10_out, out_1[10]);
  outcdecoder outcdecoder_3 (.in_1(controlled_buffer_130_out), .out_2(OutCSel));
  Decoder #(.select(3)) decoder_9 (
    .out0(_4RB_RS[0]), .out1(_4RB_RS[1]), .out2(_4RB_RS[2]), .out3(_4RB_RS[3]),
    .sel(controlled_buffer_134_out), .en(and_28_out));  // open: out4, out5, out6, out7
  and and_29 (and_29_out, out_1[7], D12_LSL, T3, not_13_out);
  assign controlled_buffer_140_out = and_29_out ? out_1[6:5] : 2'bz;  // Controlled_Buffer controlled_buffer_140
  assign MuxASel = and_29_out ? 2'b10 : 2'bz;  // Controlled_Buffer controlled_buffer_141
  assign _4RB_RS = and_29_out ? 4'b0000 : 4'bz;  // Controlled_Buffer controlled_buffer_142
  assign MuxCSel = and_29_out ? 1'b0 : 1'bz;  // Controlled_Buffer controlled_buffer_143
  assign ALUFS = and_29_out ? 4'b1010 : 4'bz;  // Controlled_Buffer controlled_buffer_144
  not not_11 (not_11_out, out_1[7]);
  not not_12 (not_12_out, out_1[7]);
  not not_13 (not_13_out, out_1[10]);
  outcdecoder outcdecoder_4 (.in_1(controlled_buffer_140_out), .out_2(OutCSel));
  and and_30 (and_30_out, not_12_out, D12_LSL, T3, not_14_out);
  assign OutASel = and_30_out ? out_1[6:5] : 2'bz;  // Controlled_Buffer controlled_buffer_145
  assign MuxCSel = and_30_out ? 1'b1 : 1'bz;  // Controlled_Buffer controlled_buffer_146
  assign ALUFS = and_30_out ? 4'b1010 : 4'bz;  // Controlled_Buffer controlled_buffer_147
  assign MuxASel = and_30_out ? 2'b11 : 2'bz;  // Controlled_Buffer controlled_buffer_148
  assign controlled_buffer_149_out = and_30_out ? out_1[10:8] : 3'bz;  // Controlled_Buffer controlled_buffer_149
  assign _4RB_FS = and_30_out ? 2'b01 : 2'bz;  // Controlled_Buffer controlled_buffer_150
  and and_31 (and_31_out, not_11_out, D8_INC, T4, not_15_out);
  assign _4RB_FS = and_31_out ? 2'b10 : 2'bz;  // Controlled_Buffer controlled_buffer_151
  Decoder #(.select(3)) decoder_10 (
    .out0(_4RB_RS[0]), .out1(_4RB_RS[1]), .out2(_4RB_RS[2]), .out3(_4RB_RS[3]),
    .sel(controlled_buffer_152_out), .en(and_31_out));  // open: out4, out5, out6, out7
  assign controlled_buffer_152_out = and_31_out ? out_1[10:8] : 3'bz;  // Controlled_Buffer controlled_buffer_152
  and and_32 (and_32_out, out_1[7], D8_INC, T4, not_16_out);
  assign _4RB_FS = and_32_out ? 2'b10 : 2'bz;  // Controlled_Buffer controlled_buffer_153
  assign controlled_buffer_154_out = and_32_out ? out_1[10:8] : 3'bz;  // Controlled_Buffer controlled_buffer_154
  Decoder #(.select(3)) decoder_11 (
    .out0(_4RB_RS[0]), .out1(_4RB_RS[1]), .out2(_4RB_RS[2]), .out3(_4RB_RS[3]),
    .sel(controlled_buffer_154_out), .en(and_32_out));  // open: out4, out5, out6, out7
  not not_14 (not_14_out, out_1[10]);
  Decoder #(.select(3)) decoder_12 (
    .out0(_4RB_RS[0]), .out1(_4RB_RS[1]), .out2(_4RB_RS[2]), .out3(_4RB_RS[3]),
    .sel(controlled_buffer_149_out), .en(and_30_out));  // open: out4, out5, out6, out7
  not not_15 (not_15_out, out_1[10]);
  not not_16 (not_16_out, out_1[10]);
  and and_33 (and_33_out, out_1[7], D12_LSL, T4, not_17_out);
  assign MuxASel = and_33_out ? 2'b11 : 2'bz;  // Controlled_Buffer controlled_buffer_155
  Decoder #(.select(3)) decoder_13 (
    .out0(_4RB_RS[0]), .out1(_4RB_RS[1]), .out2(_4RB_RS[2]), .out3(_4RB_RS[3]),
    .sel(controlled_buffer_156_out), .en(and_33_out));  // open: out4, out5, out6, out7
  assign controlled_buffer_156_out = and_33_out ? out_1[10:8] : 3'bz;  // Controlled_Buffer controlled_buffer_156
  assign _4RB_FS = and_33_out ? 2'b01 : 2'bz;  // Controlled_Buffer controlled_buffer_157
  not not_17 (not_17_out, out_1[10]);
  not not_18 (not_18_out, out_1[7]);
  and and_34 (and_34_out, out_1[7], D8_INC, T3, out_1[10]);
  outcdecoder outcdecoder_5 (.in_1(controlled_buffer_158_out), .out_2(OutCSel));
  assign controlled_buffer_158_out = and_34_out ? out_1[6:5] : 2'bz;  // Controlled_Buffer controlled_buffer_158
  assign MuxASel = and_34_out ? 2'b10 : 2'bz;  // Controlled_Buffer controlled_buffer_159
  assign MuxCSel = and_34_out ? 1'b0 : 1'bz;  // Controlled_Buffer controlled_buffer_160
  assign ALUFS = and_34_out ? 4'b0000 : 4'bz;  // Controlled_Buffer controlled_buffer_161
  assign MuxBSel = and_34_out ? 2'b11 : 2'bz;  // Controlled_Buffer controlled_buffer_162
  assign _3RB_FS = and_34_out ? 2'b01 : 2'bz;  // Controlled_Buffer controlled_buffer_163
  assign controlled_buffer_164_out = and_34_out ? out_1[9:8] : 2'bz;  // Controlled_Buffer controlled_buffer_164
  Decoder #(.select(2), .disabled(0)) decoder_14 (
    .out0(decoder_14_out0), .out1(decoder_14_out1), .out2(_3RB_RS[1]), .out3(_3RB_RS[2]),
    .sel(controlled_buffer_164_out), .en(and_34_out));
  or or_6 (_3RB_RS[0], decoder_14_out0, decoder_14_out1);
  and and_35 (and_35_out, not_18_out, D8_INC, T3, out_1[10]);
  assign OutASel = and_35_out ? out_1[6:5] : 2'bz;  // Controlled_Buffer controlled_buffer_165
  assign MuxCSel = and_35_out ? 1'b1 : 1'bz;  // Controlled_Buffer controlled_buffer_166
  assign ALUFS = and_35_out ? 4'b0000 : 4'bz;  // Controlled_Buffer controlled_buffer_167
  assign MuxBSel = and_35_out ? 2'b11 : 2'bz;  // Controlled_Buffer controlled_buffer_168
  assign controlled_buffer_169_out = and_35_out ? out_1[9:8] : 2'bz;  // Controlled_Buffer controlled_buffer_169
  assign _3RB_FS = and_35_out ? 2'b01 : 2'bz;  // Controlled_Buffer controlled_buffer_170
  not not_19 (not_19_out, out_1[7]);
  Decoder #(.select(2), .disabled(0)) decoder_15 (
    .out0(decoder_15_out0), .out1(decoder_15_out1), .out2(_3RB_RS[1]), .out3(_3RB_RS[2]),
    .sel(controlled_buffer_169_out), .en(and_35_out));
  or or_7 (_3RB_RS[0], decoder_15_out0, decoder_15_out1);
  and and_36 (and_36_out, out_1[7], D12_LSL, T3, out_1[10]);
  assign controlled_buffer_171_out = and_36_out ? out_1[6:5] : 2'bz;  // Controlled_Buffer controlled_buffer_171
  outcdecoder outcdecoder_6 (.in_1(controlled_buffer_171_out), .out_2(OutCSel));
  assign MuxASel = and_36_out ? 2'b10 : 2'bz;  // Controlled_Buffer controlled_buffer_172
  assign MuxCSel = and_36_out ? 1'b0 : 1'bz;  // Controlled_Buffer controlled_buffer_173
  assign ALUFS = and_36_out ? 4'b1010 : 4'bz;  // Controlled_Buffer controlled_buffer_174
  assign MuxBSel = and_36_out ? 2'b11 : 2'bz;  // Controlled_Buffer controlled_buffer_175
  assign _3RB_FS = and_36_out ? 2'b01 : 2'bz;  // Controlled_Buffer controlled_buffer_176
  Decoder #(.select(2), .disabled(0)) decoder_16 (
    .out0(decoder_16_out0), .out1(decoder_16_out1), .out2(_3RB_RS[1]), .out3(_3RB_RS[2]),
    .sel(controlled_buffer_177_out), .en(and_36_out));
  assign controlled_buffer_177_out = and_36_out ? out_1[9:8] : 2'bz;  // Controlled_Buffer controlled_buffer_177
  or or_8 (_3RB_RS[0], decoder_16_out0, decoder_16_out1);
  and and_37 (and_37_out, not_19_out, D12_LSL, T3, out_1[10]);
  assign OutASel = and_37_out ? out_1[6:5] : 2'bz;  // Controlled_Buffer controlled_buffer_178
  assign MuxCSel = and_37_out ? 1'b1 : 1'bz;  // Controlled_Buffer controlled_buffer_179
  assign ALUFS = and_37_out ? 4'b1010 : 4'bz;  // Controlled_Buffer controlled_buffer_180
  assign MuxBSel = and_37_out ? 2'b11 : 2'bz;  // Controlled_Buffer controlled_buffer_181
  assign controlled_buffer_182_out = and_37_out ? out_1[9:8] : 2'bz;  // Controlled_Buffer controlled_buffer_182
  assign _3RB_FS = and_37_out ? 2'b01 : 2'bz;  // Controlled_Buffer controlled_buffer_183
  not not_20 (not_20_out, out_1[7]);
  Decoder #(.select(2), .disabled(0)) decoder_17 (
    .out0(decoder_17_out0), .out1(decoder_17_out1), .out2(_3RB_RS[1]), .out3(_3RB_RS[2]),
    .sel(controlled_buffer_182_out), .en(and_37_out));
  or or_9 (_3RB_RS[0], decoder_17_out0, decoder_17_out1);
  and and_38 (and_38_out, out_1[7], D8_INC, T4, out_1[10]);
  assign _3RB_FS = and_38_out ? 2'b10 : 2'bz;  // Controlled_Buffer controlled_buffer_184
  Decoder #(.select(2), .disabled(0)) decoder_18 (
    .out0(decoder_18_out0), .out1(decoder_18_out1), .out2(_3RB_RS[1]), .out3(_3RB_RS[2]),
    .sel(controlled_buffer_185_out), .en(and_38_out));
  assign controlled_buffer_185_out = and_38_out ? out_1[9:8] : 2'bz;  // Controlled_Buffer controlled_buffer_185
  or or_10 (_3RB_RS[0], decoder_18_out0, decoder_18_out1);
  and and_39 (and_39_out, not_20_out, D8_INC, T4, out_1[10]);
  assign _3RB_FS = and_39_out ? 2'b10 : 2'bz;  // Controlled_Buffer controlled_buffer_186
  assign controlled_buffer_187_out = and_39_out ? out_1[9:8] : 2'bz;  // Controlled_Buffer controlled_buffer_187
  Decoder #(.select(2), .disabled(0)) decoder_19 (
    .out0(decoder_19_out0), .out1(decoder_19_out1), .out2(_3RB_RS[1]), .out3(_3RB_RS[2]),
    .sel(controlled_buffer_187_out), .en(and_39_out));
  or or_11 (_3RB_RS[0], decoder_19_out0, decoder_19_out1);
  not not_21 (not_21_out, out_1[7]);
  or or_12 (or_12_out, not_21_out, and_40_out);
  and and_40 (and_40_out, out_1[7], out_1[10]);
  and and_41 (and_41_out, or_12_out, D12_LSL, T4);
  assign SCR = and_41_out ? 1'b1 : 1'bz;  // Controlled_Buffer controlled_buffer_188
  and and_42 (and_42_out, out_1[7], D12_LSL, T5, not_22_out);
  assign SCR = and_42_out ? 1'b1 : 1'bz;  // Controlled_Buffer controlled_buffer_189
  and and_43 (and_43_out, D8_INC, T5);
  assign SCR = and_43_out ? 1'b1 : 1'bz;  // Controlled_Buffer controlled_buffer_190
  not not_22 (not_22_out, out_1[10]);
  assign MEM_SEL = D7_DEC ? 1'b0 : 1'bz;  // Controlled_Buffer controlled_buffer_191
  assign MEM_LD = D7_DEC ? 1'b0 : 1'bz;  // Controlled_Buffer controlled_buffer_192
  assign MEM_STR = D7_DEC ? 1'b0 : 1'bz;  // Controlled_Buffer controlled_buffer_193
  assign MEM_CLR = D7_DEC ? 1'b0 : 1'bz;  // Controlled_Buffer controlled_buffer_194
  assign MEM_SEL = D13_LSR ? 1'b0 : 1'bz;  // Controlled_Buffer controlled_buffer_195
  assign MEM_LD = D13_LSR ? 1'b0 : 1'bz;  // Controlled_Buffer controlled_buffer_196
  assign MEM_STR = D13_LSR ? 1'b0 : 1'bz;  // Controlled_Buffer controlled_buffer_197
  assign MEM_CLR = D13_LSR ? 1'b0 : 1'bz;  // Controlled_Buffer controlled_buffer_198
  not not_23 (not_23_out, out_1[7]);
  and and_44 (and_44_out, out_1[7], D13_LSR, T3, not_25_out);
  assign controlled_buffer_199_out = and_44_out ? out_1[6:5] : 2'bz;  // Controlled_Buffer controlled_buffer_199
  assign MuxASel = and_44_out ? 2'b10 : 2'bz;  // Controlled_Buffer controlled_buffer_200
  assign _4RB_RS = and_44_out ? 4'b0000 : 4'bz;  // Controlled_Buffer controlled_buffer_201
  assign MuxCSel = and_44_out ? 1'b0 : 1'bz;  // Controlled_Buffer controlled_buffer_202
  assign ALUFS = and_44_out ? 4'b1011 : 4'bz;  // Controlled_Buffer controlled_buffer_203
  and and_45 (and_45_out, not_23_out, D7_DEC, T3, not_26_out);
  assign OutASel = and_45_out ? out_1[6:5] : 2'bz;  // Controlled_Buffer controlled_buffer_204
  assign MuxCSel = and_45_out ? 1'b1 : 1'bz;  // Controlled_Buffer controlled_buffer_205
  assign ALUFS = and_45_out ? 4'b0000 : 4'bz;  // Controlled_Buffer controlled_buffer_206
  assign MuxASel = and_45_out ? 2'b11 : 2'bz;  // Controlled_Buffer controlled_buffer_207
  assign controlled_buffer_208_out = and_45_out ? out_1[10:8] : 3'bz;  // Controlled_Buffer controlled_buffer_208
  assign _4RB_FS = and_45_out ? 2'b01 : 2'bz;  // Controlled_Buffer controlled_buffer_209
  and and_46 (and_46_out, out_1[7], D7_DEC, T3, not_27_out);
  assign controlled_buffer_210_out = and_46_out ? out_1[6:5] : 2'bz;  // Controlled_Buffer controlled_buffer_210
  assign MuxASel = and_46_out ? 2'b10 : 2'bz;  // Controlled_Buffer controlled_buffer_211
  assign MuxCSel = and_46_out ? 1'b0 : 1'bz;  // Controlled_Buffer controlled_buffer_212
  assign _4RB_FS = and_46_out ? 2'b01 : 2'bz;  // Controlled_Buffer controlled_buffer_213
  assign controlled_buffer_214_out = and_46_out ? out_1[10:8] : 3'bz;  // Controlled_Buffer controlled_buffer_214
  assign _4RB_FS = and_46_out ? 2'b01 : 2'bz;  // Controlled_Buffer controlled_buffer_215
  not not_24 (not_24_out, out_1[7]);
  not not_25 (not_25_out, out_1[10]);
  outcdecoder outcdecoder_7 (.in_1(controlled_buffer_199_out), .out_2(OutCSel));
  not not_26 (not_26_out, out_1[10]);
  Decoder #(.select(3)) decoder_20 (
    .out0(_4RB_RS[0]), .out1(_4RB_RS[1]), .out2(_4RB_RS[2]), .out3(_4RB_RS[3]),
    .sel(controlled_buffer_208_out), .en(and_45_out));  // open: out4, out5, out6, out7
  not not_27 (not_27_out, out_1[10]);
  outcdecoder outcdecoder_8 (.in_1(controlled_buffer_210_out), .out_2(OutCSel));
  Decoder #(.select(3)) decoder_21 (
    .out0(_4RB_RS[0]), .out1(_4RB_RS[1]), .out2(_4RB_RS[2]), .out3(_4RB_RS[3]),
    .sel(controlled_buffer_214_out), .en(and_46_out));  // open: out4, out5, out6, out7
  and and_47 (and_47_out, not_24_out, D13_LSR, T3, not_29_out);
  assign OutASel = and_47_out ? out_1[6:5] : 2'bz;  // Controlled_Buffer controlled_buffer_216
  assign MuxCSel = and_47_out ? 1'b1 : 1'bz;  // Controlled_Buffer controlled_buffer_217
  assign ALUFS = and_47_out ? 4'b1011 : 4'bz;  // Controlled_Buffer controlled_buffer_218
  assign MuxASel = and_47_out ? 2'b11 : 2'bz;  // Controlled_Buffer controlled_buffer_219
  assign controlled_buffer_220_out = and_47_out ? out_1[10:8] : 3'bz;  // Controlled_Buffer controlled_buffer_220
  assign _4RB_FS = and_47_out ? 2'b01 : 2'bz;  // Controlled_Buffer controlled_buffer_221
  not not_28 (not_28_out, out_1[7]);
  not not_29 (not_29_out, out_1[10]);
  Decoder #(.select(3)) decoder_22 (
    .out0(_4RB_RS[0]), .out1(_4RB_RS[1]), .out2(_4RB_RS[2]), .out3(_4RB_RS[3]),
    .sel(controlled_buffer_220_out), .en(and_47_out));  // open: out4, out5, out6, out7
  and and_48 (and_48_out, out_1[7], D13_LSR, T4, not_30_out);
  assign MuxASel = and_48_out ? 2'b11 : 2'bz;  // Controlled_Buffer controlled_buffer_222
  assign controlled_buffer_223_out = and_48_out ? out_1[10:8] : 3'bz;  // Controlled_Buffer controlled_buffer_223
  Decoder #(.select(3)) decoder_23 (
    .out0(_4RB_RS[0]), .out1(_4RB_RS[1]), .out2(_4RB_RS[2]), .out3(_4RB_RS[3]),
    .sel(controlled_buffer_223_out), .en(and_48_out));  // open: out4, out5, out6, out7
  assign _4RB_FS = and_48_out ? 2'b01 : 2'bz;  // Controlled_Buffer controlled_buffer_224
  and and_49 (and_49_out, not_28_out, D7_DEC, T4, not_31_out);
  assign _4RB_FS = and_49_out ? 2'b11 : 2'bz;  // Controlled_Buffer controlled_buffer_225
  assign controlled_buffer_226_out = and_49_out ? out_1[10:8] : 3'bz;  // Controlled_Buffer controlled_buffer_226
  Decoder #(.select(3)) decoder_24 (
    .out0(_4RB_RS[0]), .out1(_4RB_RS[1]), .out2(_4RB_RS[2]), .out3(_4RB_RS[3]),
    .sel(controlled_buffer_226_out), .en(and_49_out));  // open: out4, out5, out6, out7
  and and_50 (and_50_out, out_1[7], D7_DEC, T4, not_32_out);
  assign _4RB_FS = and_50_out ? 2'b11 : 2'bz;  // Controlled_Buffer controlled_buffer_227
  Decoder #(.select(3)) decoder_25 (
    .out0(_4RB_RS[0]), .out1(_4RB_RS[1]), .out2(_4RB_RS[2]), .out3(_4RB_RS[3]),
    .sel(controlled_buffer_228_out), .en(and_50_out));  // open: out4, out5, out6, out7
  assign controlled_buffer_228_out = and_50_out ? out_1[10:8] : 3'bz;  // Controlled_Buffer controlled_buffer_228
  not not_30 (not_30_out, out_1[10]);
  not not_31 (not_31_out, out_1[10]);
  not not_32 (not_32_out, out_1[10]);
  not not_33 (not_33_out, out_1[7]);
  not not_34 (not_34_out, out_1[7]);
  and and_51 (and_51_out, out_1[7], D13_LSR, T3, out_1[10]);
  outcdecoder outcdecoder_9 (.in_1(controlled_buffer_229_out), .out_2(OutCSel));
  assign controlled_buffer_229_out = and_51_out ? out_1[6:5] : 2'bz;  // Controlled_Buffer controlled_buffer_229
  assign MuxASel = and_51_out ? 2'b10 : 2'bz;  // Controlled_Buffer controlled_buffer_230
  assign MuxCSel = and_51_out ? 1'b0 : 1'bz;  // Controlled_Buffer controlled_buffer_231
  assign ALUFS = and_51_out ? 4'b1011 : 4'bz;  // Controlled_Buffer controlled_buffer_232
  assign MuxBSel = and_51_out ? 2'b11 : 2'bz;  // Controlled_Buffer controlled_buffer_233
  assign _3RB_FS = and_51_out ? 2'b01 : 2'bz;  // Controlled_Buffer controlled_buffer_234
  assign controlled_buffer_235_out = and_51_out ? out_1[9:8] : 2'bz;  // Controlled_Buffer controlled_buffer_235
  Decoder #(.select(2), .disabled(0)) decoder_26 (
    .out0(decoder_26_out0), .out1(decoder_26_out1), .out2(_3RB_RS[1]), .out3(_3RB_RS[2]),
    .sel(controlled_buffer_235_out), .en(and_51_out));
  or or_13 (_3RB_RS[0], decoder_26_out0, decoder_26_out1);
  and and_52 (and_52_out, not_33_out, D13_LSR, T3, out_1[10]);
  assign OutASel = and_52_out ? out_1[6:5] : 2'bz;  // Controlled_Buffer controlled_buffer_236
  assign MuxCSel = and_52_out ? 1'b1 : 1'bz;  // Controlled_Buffer controlled_buffer_237
  assign ALUFS = and_52_out ? 4'b1011 : 4'bz;  // Controlled_Buffer controlled_buffer_238
  assign MuxBSel = and_52_out ? 2'b11 : 2'bz;  // Controlled_Buffer controlled_buffer_239
  assign controlled_buffer_240_out = and_52_out ? out_1[9:8] : 2'bz;  // Controlled_Buffer controlled_buffer_240
  assign _3RB_FS = and_52_out ? 2'b01 : 2'bz;  // Controlled_Buffer controlled_buffer_241
  and and_53 (and_53_out, out_1[7], D7_DEC, T3, out_1[10]);
  assign controlled_buffer_242_out = and_53_out ? out_1[6:5] : 2'bz;  // Controlled_Buffer controlled_buffer_242
  assign MuxASel = and_53_out ? 2'b10 : 2'bz;  // Controlled_Buffer controlled_buffer_243
  assign MuxCSel = and_53_out ? 1'b0 : 1'bz;  // Controlled_Buffer controlled_buffer_244
  assign ALUFS = and_53_out ? 4'b0000 : 4'bz;  // Controlled_Buffer controlled_buffer_245
  assign MuxBSel = and_53_out ? 2'b11 : 2'bz;  // Controlled_Buffer controlled_buffer_246
  assign _3RB_FS = and_53_out ? 2'b01 : 2'bz;  // Controlled_Buffer controlled_buffer_247
  assign controlled_buffer_248_out = and_53_out ? out_1[9:8] : 2'bz;  // Controlled_Buffer controlled_buffer_248
  and and_54 (and_54_out, not_34_out, D7_DEC, T3, out_1[10]);
  assign OutASel = and_54_out ? out_1[6:5] : 2'bz;  // Controlled_Buffer controlled_buffer_249
  assign MuxCSel = and_54_out ? 1'b1 : 1'bz;  // Controlled_Buffer controlled_buffer_250
  assign ALUFS = and_54_out ? 4'b0000 : 4'bz;  // Controlled_Buffer controlled_buffer_251
  assign MuxBSel = and_54_out ? 2'b11 : 2'bz;  // Controlled_Buffer controlled_buffer_252
  assign controlled_buffer_253_out = and_54_out ? out_1[9:8] : 2'bz;  // Controlled_Buffer controlled_buffer_253
  assign _3RB_FS = and_54_out ? 2'b01 : 2'bz;  // Controlled_Buffer controlled_buffer_254
  Decoder #(.select(2), .disabled(0)) decoder_27 (
    .out0(decoder_27_out0), .out1(decoder_27_out1), .out2(_3RB_RS[1]), .out3(_3RB_RS[2]),
    .sel(controlled_buffer_240_out), .en(and_52_out));
  or or_14 (_3RB_RS[0], decoder_27_out0, decoder_27_out1);
  outcdecoder outcdecoder_10 (.in_1(controlled_buffer_242_out), .out_2(OutCSel));
  Decoder #(.select(2), .disabled(0)) decoder_28 (
    .out0(decoder_28_out0), .out1(decoder_28_out1), .out2(_3RB_RS[1]), .out3(_3RB_RS[2]),
    .sel(controlled_buffer_248_out), .en(and_53_out));
  or or_15 (_3RB_RS[0], decoder_28_out0, decoder_28_out1);
  Decoder #(.select(2), .disabled(0)) decoder_29 (
    .out0(decoder_29_out0), .out1(decoder_29_out1), .out2(_3RB_RS[1]), .out3(_3RB_RS[2]),
    .sel(controlled_buffer_253_out), .en(and_54_out));
  or or_16 (_3RB_RS[0], decoder_29_out0, decoder_29_out1);
  not not_35 (not_35_out, out_1[7]);
  not not_36 (not_36_out, out_1[7]);
  or or_17 (or_17_out, not_36_out, and_55_out);
  and and_55 (and_55_out, out_1[7], out_1[10]);
  and and_56 (and_56_out, or_17_out, D13_LSR, T4);
  assign SCR = and_56_out ? 1'b1 : 1'bz;  // Controlled_Buffer controlled_buffer_255
  and and_57 (and_57_out, out_1[7], D13_LSR, T5, not_37_out);
  assign SCR = and_57_out ? 1'b1 : 1'bz;  // Controlled_Buffer controlled_buffer_256
  and and_58 (and_58_out, out_1[7], D7_DEC, T4, out_1[10]);
  assign _3RB_FS = and_58_out ? 2'b11 : 2'bz;  // Controlled_Buffer controlled_buffer_257
  Decoder #(.select(2), .disabled(0)) decoder_30 (
    .out0(decoder_30_out0), .out1(decoder_30_out1), .out2(_3RB_RS[1]), .out3(_3RB_RS[2]),
    .sel(controlled_buffer_258_out), .en(and_58_out));
  assign controlled_buffer_258_out = and_58_out ? out_1[9:8] : 2'bz;  // Controlled_Buffer controlled_buffer_258
  or or_18 (_3RB_RS[0], decoder_30_out0, decoder_30_out1);
  and and_59 (and_59_out, not_35_out, D7_DEC, T4, out_1[10]);
  assign _3RB_FS = and_59_out ? 2'b11 : 2'bz;  // Controlled_Buffer controlled_buffer_259
  assign controlled_buffer_260_out = and_59_out ? out_1[9:8] : 2'bz;  // Controlled_Buffer controlled_buffer_260
  Decoder #(.select(2), .disabled(0)) decoder_31 (
    .out0(decoder_31_out0), .out1(decoder_31_out1), .out2(_3RB_RS[1]), .out3(_3RB_RS[2]),
    .sel(controlled_buffer_260_out), .en(and_59_out));
  or or_19 (_3RB_RS[0], decoder_31_out0, decoder_31_out1);
  not not_37 (not_37_out, out_1[10]);
  and and_60 (and_60_out, D7_DEC, T5);
  assign SCR = and_60_out ? 1'b1 : 1'bz;  // Controlled_Buffer controlled_buffer_261

  // Other names for the same wires on the sheet: ADDRESS[7:0] = out_1[7:0]; INSTR[15:0] = out_1;
  //   SRCREG2[2:0] = out_1[4:2]; SRCREG1[2:0] = out_1[7:5]; AdrMOD = out_1[8]; DESTREG[2:0] = out_1[10:8];
  //   REGSEL[1:0] = out_1[10:9]; OPCODE[4:0] = out_1[15:11]

  // Notes on the sheet:
  //   BRA
  //   MOV
  //   LD
  //   BEQ & BNE
  //   CALL
  //   RET
  //   ST
  //   ADD
  //   4RB TO 4RB
  //   3RB TO 4RB
  //   4RB TO 4RB
  //   3RB TO 4RB
  //   INC
  //   LSL
  //   3RB TO 3RB
  //   4RB TO 3RB
  //   3RB TO 3RB
  //   4RB TO 3RB
  //   IF NOT 3RB to 4RB
  //   IF 3RB to 4RB
  //   4RB TO 4RB
  //   3RB TO 4RB
  //   4RB TO 4RB
  //   3RB TO 4RB
  //   DEC
  //   LSR
  //   3RB TO 3RB
  //   4RB TO 3RB
  //   3RB TO 3RB
  //   4RB TO 3RB
  //   IF NOT 3RB to 4RB
  //   IF 3RB to 4RB
endmodule

module counter (
  input  in_1,
  output out_2,
  output out_3,
  output out_4,
  output out_5,
  output out_6,
  output out_7,
  output out_8,
  output out_9
);

  wire clock_1_out;
  wire [2:0] counter_1_q;

  Counter #(.width(3), .max('h7)) counter_1 (
    .Q(counter_1_q), .clk(clock_1_out), .clr(in_1));  // open: load, D, count, carry
  Clock clock_1 (.out(clock_1_out));
  Decoder #(.select(3), .enable("false")) decoder_1 (
    .out0(out_2), .out1(out_3), .out2(out_4), .out3(out_5), .out4(out_6), .out5(out_7), .out6(out_8),
    .out7(out_9), .sel(counter_1_q));
endmodule

module outcdecoder (
  input  [1:0] in_1,
  output [1:0] out_2
);

  Subtractor #(.width(2)) subtractor_1 (.a(in_1), .b(2'b01), .out(out_2));  // open: bin, bout
endmodule
